// Digital circuit cpu.dig as structural Verilog
module cpu (
  input  ACASCADEMOD,
  input  AINMOD,
  input  AENO,
  input  ALUCIN,
  input  ALOAD,
  input  ACLKMOD,
  input  ALUENO,
  input  CLK,
  input  AENDEF,
  input  BCASCADEMOD,
  input  BINMOD,
  input  BENO,
  input  BLOAD,
  input  BCLKMOD,
  input  BENDEF,
  input  EN,
  input  D0,
  input  D1,
  input  D2,
  input  D3,
  input  D4,
  input  D5,
  input  D6,
  input  D7,
  input  PCCASCADEMOD,
  input  PCINMOD,
  input  PCENO,
  input  PCLOAD,
  input  PCCLKMOD,
  input  PCENDEF,
  input  MARCASCADEMOD,
  input  MARINMOD,
  input  MARLOAD,
  input  MARCLKMOD,
  input  MARENDEF,
  input  IRLOAD,
  input  IRENO,
  input  RAMENO,
  input  RAMLOAD,
  input  in_40,
  input  MARENO,
  input  FEN,
  input  ACNTRLLINEMOD,
  input  BCNTRLLINEMOD,
  input  AND,
  input  MARPCPRIVBUS,
  output out_42
);

  wire add_1_c_o, add_1_s, add_2_c_o, add_2_s, add_3_c_o, add_3_s, add_4_c_o, add_4_s, add_5_c_o, add_5_s,
       add_6_c_o, add_6_s, add_7_c_o, add_7_s, add_8_c_o, add_8_s, and_1_out, and_2_out, and_3_out,
       and_4_out, and_5_out, and_6_out, and_7_out, and_8_out, and_9_out, and_10_out, and_11_out, and_12_out,
       and_13_out, and_14_out, and_15_out, and_16_out, and_17_out, and_18_out, and_19_out, and_20_out,
       and_21_out, and_22_out, and_23_out, and_24_out, and_25_out, and_26_out, and_27_out, and_28_out,
       and_29_out, and_30_out, and_31_out, and_32_out, and_33_out, and_34_out, and_35_out, and_36_out,
       and_37_out, and_38_out, and_39_out, and_40_out, and_41_out, and_42_out, d_ff_1_q, d_ff_2_q, d_ff_3_q,
       d_ff_4_q, d_ff_9_q, d_ff_10_q, decoder_1_out_0, decoder_1_out_1, decoder_1_out_2, decoder_1_out_3,
       decoder_2_out_0, decoder_2_out_1, decoder_2_out_2, decoder_2_out_4, decoder_2_out_5, decoder_2_out_6,
       decoder_2_out_7, decoder_3_out_0, decoder_3_out_1, decoder_3_out_2, decoder_3_out_4, decoder_3_out_5,
       decoder_3_out_6, decoder_3_out_7, delay_1_out, delay_2_out, delay_3_out, delay_4_out, delay_5_out,
       delay_6_out, delay_7_out, delay_8_out, demultiplexer_3_out_1, demultiplexer_3_out_2,
       demultiplexer_3_out_3, demultiplexer_3_out_5, demultiplexer_3_out_6, demultiplexer_3_out_7,
       jk_ff_1_nq, jk_ff_2_nq, jk_ff_3_nq, jk_ff_4_nq, jk_ff_5_nq, jk_ff_6_nq, jk_ff_7_nq, jk_ff_9_nq,
       jk_ff_9_q, jk_ff_10_nq, jk_ff_10_q, jk_ff_11_nq, jk_ff_11_q, jk_ff_12_nq, jk_ff_12_q, jk_ff_13_nq,
       jk_ff_13_q, jk_ff_14_nq, jk_ff_14_q, jk_ff_15_nq, jk_ff_15_q, jk_ff_16_q, jk_ff_17_nq, jk_ff_17_q,
       jk_ff_18_nq, jk_ff_18_q, jk_ff_19_nq, jk_ff_19_q, jk_ff_20_nq, jk_ff_20_q, jk_ff_21_nq, jk_ff_21_q,
       jk_ff_22_nq, jk_ff_22_q, jk_ff_23_nq, jk_ff_23_q, jk_ff_24_q, jk_ff_25_nq, jk_ff_25_q, jk_ff_26_nq,
       jk_ff_26_q, jk_ff_27_nq, jk_ff_27_q, jk_ff_28_nq, jk_ff_28_q, jk_ff_29_nq, jk_ff_29_q, jk_ff_30_nq,
       jk_ff_30_q, jk_ff_31_nq, jk_ff_31_q, jk_ff_32_q, multiplexer_1_out, multiplexer_2_out,
       multiplexer_3_out, multiplexer_4_out, multiplexer_5_out, multiplexer_6_out, multiplexer_7_out,
       multiplexer_8_out, multiplexer_9_out, multiplexer_10_out, multiplexer_11_out, multiplexer_12_out,
       multiplexer_13_out, multiplexer_14_out, multiplexer_15_out, multiplexer_16_out, multiplexer_18_out,
       multiplexer_19_out, multiplexer_20_out, multiplexer_21_out, multiplexer_22_out, multiplexer_23_out,
       multiplexer_24_out, multiplexer_25_out, multiplexer_26_out, multiplexer_27_out, multiplexer_28_out,
       multiplexer_29_out, multiplexer_30_out, multiplexer_31_out, multiplexer_32_out, multiplexer_34_out,
       multiplexer_36_out, multiplexer_37_out, multiplexer_38_out, multiplexer_40_out, multiplexer_41_out,
       multiplexer_42_out, multiplexer_43_out, multiplexer_44_out, multiplexer_45_out, multiplexer_46_out,
       multiplexer_47_out, multiplexer_48_out, multiplexer_49_out, multiplexer_50_out, multiplexer_51_out,
       multiplexer_52_out, multiplexer_55_out, multiplexer_56_out, multiplexer_57_out, multiplexer_58_out,
       multiplexer_59_out, multiplexer_60_out, multiplexer_61_out, multiplexer_62_out, multiplexer_63_out,
       multiplexer_64_out, multiplexer_65_out, multiplexer_66_out, multiplexer_67_out, multiplexer_68_out,
       multiplexer_69_out, multiplexer_70_out, multiplexer_71_out, multiplexer_72_out, multiplexer_73_out,
       multiplexer_74_out, multiplexer_75_out, multiplexer_76_out, multiplexer_77_out, multiplexer_78_out,
       multiplexer_79_out, multiplexer_80_out, multiplexer_81_out, multiplexer_82_out, multiplexer_83_out,
       multiplexer_84_out, multiplexer_85_out, multiplexer_86_out, multiplexer_87_out, multiplexer_88_out,
       multiplexer_89_out, multiplexer_90_out, multiplexer_91_out, multiplexer_92_out, multiplexer_93_out,
       multiplexer_94_out, multiplexer_96_out, multiplexer_97_out, multiplexer_98_out, multiplexer_99_out,
       multiplexer_100_out, multiplexer_101_out, multiplexer_102_out, multiplexer_103_out,
       multiplexer_105_out, multiplexer_106_out, multiplexer_107_out, multiplexer_108_out,
       multiplexer_109_out, multiplexer_110_out, multiplexer_111_out, multiplexer_112_out,
       multiplexer_113_out, multiplexer_114_out, multiplexer_115_out, multiplexer_116_out,
       multiplexer_117_out, multiplexer_118_out, multiplexer_119_out, multiplexer_120_out,
       multiplexer_121_out, multiplexer_122_out, multiplexer_123_out, multiplexer_124_out,
       multiplexer_125_out, multiplexer_126_out, multiplexer_127_out, multiplexer_128_out,
       multiplexer_129_out, multiplexer_130_out, multiplexer_131_out, multiplexer_132_out,
       multiplexer_133_out, multiplexer_134_out, multiplexer_135_out, multiplexer_136_out,
       multiplexer_137_out, multiplexer_138_out, multiplexer_139_out, multiplexer_140_out,
       multiplexer_141_out, multiplexer_142_out, multiplexer_143_out, multiplexer_144_out,
       multiplexer_145_out, multiplexer_146_out, multiplexer_147_out, multiplexer_148_out,
       multiplexer_149_out, multiplexer_150_out, multiplexer_151_out, multiplexer_152_out,
       multiplexer_153_out, multiplexer_154_out, multiplexer_155_out, multiplexer_156_out,
       multiplexer_157_out, multiplexer_158_out, multiplexer_159_out, multiplexer_160_out,
       multiplexer_161_out, multiplexer_162_out, multiplexer_163_out, multiplexer_164_out,
       multiplexer_165_out, multiplexer_166_out, multiplexer_167_out, multiplexer_168_out, nor_1_out,
       nor_2_out, nor_3_out, nor_4_out, not_1_out, not_2_out, not_3_out, not_4_out, not_5_out, not_6_out,
       not_7_out, not_8_out, not_9_out, not_10_out, not_11_out, not_12_out, not_13_out, not_14_out,
       not_15_out, not_16_out, not_17_out, not_18_out, not_19_out, not_20_out, not_21_out, not_22_out,
       not_23_out, not_24_out, not_25_out, not_26_out, not_27_out, not_28_out, or_1_out, or_3_out, or_4_out,
       or_5_out, or_6_out, or_7_out, or_8_out, or_9_out, or_10_out, or_11_out, or_12_out, or_13_out,
       or_14_out, or_15_out, or_16_out, or_17_out, or_18_out, pulldown_1_out, pulldown_2_out, pulldown_9_out,
       pulldown_10_out, pulldown_27_out, pulldown_30_out, pulldown_32_out, pulldown_34_out, xor_1_out,
       xor_2_out, xor_3_out, xor_4_out, xor_5_out, xor_6_out, xor_7_out, xor_8_out, xor_9_out, xor_10_out,
       xor_11_out, xor_12_out, xor_13_out, xor_14_out, xor_15_out, xor_16_out, xor_17_out, xor_18_out,
       xor_19_out, xor_20_out, xor_21_out, xor_22_out, xor_23_out, xor_24_out, xor_25_out, xor_26_out,
       xor_27_out, xor_28_out, xor_29_out, xor_30_out, xor_31_out, xor_32_out;
  wire [1:0] counter_1_out;
  wire [2:1] multiplexer_95_out;
  wire [4:0] d_ff_5_q;
  wire [7:0] demultiplexer_1_out_0, demultiplexer_1_out_1, demultiplexer_2_out_0, demultiplexer_2_out_1,
       driver_8_out, driver_11_out, driver_66_out, jk_ff_5_q, multiplexer_53_out, multiplexer_54_out,
       ramdualport_1_d;
  wire [30:0] pulldown_43_out;

  Multiplexer multiplexer_1 (
    .sel(pulldown_43_out[5]), .in_0(multiplexer_53_out[7]), .in_1(1'b1), .out(multiplexer_1_out));
  Multiplexer multiplexer_2 (
    .sel(pulldown_43_out[5]), .in_0(multiplexer_53_out[6]), .in_1(1'b1), .out(multiplexer_2_out));
  Multiplexer multiplexer_3 (
    .sel(pulldown_43_out[5]), .in_0(multiplexer_53_out[5]), .in_1(1'b1), .out(multiplexer_3_out));
  Multiplexer multiplexer_4 (
    .sel(pulldown_43_out[5]), .in_0(multiplexer_53_out[4]), .in_1(1'b1), .out(multiplexer_4_out));
  Multiplexer multiplexer_5 (
    .sel(pulldown_43_out[5]), .in_0(multiplexer_53_out[3]), .in_1(1'b1), .out(multiplexer_5_out));
  Multiplexer multiplexer_6 (
    .sel(pulldown_43_out[5]), .in_0(multiplexer_53_out[2]), .in_1(1'b1), .out(multiplexer_6_out));
  Multiplexer multiplexer_7 (
    .sel(pulldown_43_out[5]), .in_0(multiplexer_53_out[1]), .in_1(1'b1), .out(multiplexer_7_out));
  Multiplexer multiplexer_8 (
    .sel(pulldown_43_out[5]), .in_0(multiplexer_53_out[0]), .in_1(1'b1), .out(multiplexer_8_out));
  Counter #(.Bits(2)) counter_1 (.en(in_40), .C(not_1_out), .clr(not_2_out), .out(counter_1_out));  // open: ovf
  not not_1 (not_1_out, CLK);
  not not_2 (not_2_out, in_40);
  and and_1 (and_1_out, decoder_1_out_3, in_40);
  or or_1 (or_1_out, and_3_out, and_1_out);
  not not_3 (not_3_out, or_1_out);
  not not_4 (not_4_out, not_3_out);
  and and_2 (and_2_out, pulldown_43_out[4], or_5_out);
  not not_5 (not_5_out, and_2_out);
  and and_3 (and_3_out, in_40, decoder_1_out_2);
  Multiplexer multiplexer_9 (.sel(or_5_out), .in_0(jk_ff_5_q[0]), .in_1(multiplexer_1_out), .out(multiplexer_9_out));
  Multiplexer multiplexer_10 (.sel(or_5_out), .in_0(jk_ff_5_q[1]), .in_1(multiplexer_2_out), .out(multiplexer_10_out));
  Multiplexer multiplexer_11 (.sel(or_5_out), .in_0(jk_ff_5_q[2]), .in_1(multiplexer_3_out), .out(multiplexer_11_out));
  Multiplexer multiplexer_12 (.sel(or_5_out), .in_0(jk_ff_5_q[3]), .in_1(multiplexer_4_out), .out(multiplexer_12_out));
  Multiplexer multiplexer_13 (.sel(or_5_out), .in_0(jk_ff_5_q[4]), .in_1(multiplexer_5_out), .out(multiplexer_13_out));
  Multiplexer multiplexer_14 (.sel(or_5_out), .in_0(jk_ff_5_q[5]), .in_1(multiplexer_6_out), .out(multiplexer_14_out));
  Multiplexer multiplexer_15 (.sel(or_5_out), .in_0(jk_ff_5_q[6]), .in_1(multiplexer_7_out), .out(multiplexer_15_out));
  Multiplexer multiplexer_16 (.sel(or_5_out), .in_0(jk_ff_5_q[7]), .in_1(multiplexer_8_out), .out(multiplexer_16_out));
  Decoder #(.Selector_Bits(2)) decoder_1 (
    .sel(counter_1_out), .out_0(decoder_1_out_0), .out_1(decoder_1_out_1), .out_2(decoder_1_out_2),
    .out_3(decoder_1_out_3));
  and and_4 (and_4_out, in_40, decoder_1_out_1);
  Multiplexer multiplexer_17 (.sel(and_4_out), .in_0(pulldown_1_out), .in_1(and_4_out), .out(pulldown_43_out[30]));
  PullDown pulldown_1 (.out(pulldown_1_out));
  PullDown pulldown_2 (.out(pulldown_2_out));
  Multiplexer multiplexer_18 (.sel(and_4_out), .in_0(pulldown_2_out), .in_1(and_4_out), .out(multiplexer_18_out));
  xor xor_1 (xor_1_out, multiplexer_9_out, not_5_out);
  xor xor_2 (xor_2_out, multiplexer_10_out, not_5_out);
  xor xor_3 (xor_3_out, multiplexer_11_out, not_5_out);
  xor xor_4 (xor_4_out, multiplexer_12_out, not_5_out);
  xor xor_5 (xor_5_out, multiplexer_13_out, not_5_out);
  xor xor_6 (xor_6_out, multiplexer_14_out, not_5_out);
  xor xor_7 (xor_7_out, multiplexer_15_out, not_5_out);
  xor xor_8 (xor_8_out, multiplexer_16_out, not_5_out);
  and and_5 (and_5_out, in_40, decoder_1_out_0);
  PullDown pulldown_3 (.out(pulldown_43_out[29]));
  PullDown pulldown_4 (.out(pulldown_43_out[30]));
  or or_2 (d_ff_5_q[4], and_1_out, not_6_out);
  not not_6 (not_6_out, and_3_out);
  and and_6 (and_6_out, and_3_out, or_3_out);
  and and_7 (and_7_out, and_1_out, or_3_out);
  PullDown pulldown_5 (.out(pulldown_43_out[25]));
  PullDown pulldown_6 (.out(pulldown_43_out[26]));
  PullDown pulldown_7 (.out(pulldown_43_out[27]));
  PullDown pulldown_8 (.out(pulldown_43_out[28]));
  Delay delay_1 (.in(CLK), .out(delay_1_out));
  Delay #(.delayTime(5)) delay_2 (.in(delay_1_out), .out(delay_2_out));
  Delay #(.delayTime(5)) delay_3 (.in(delay_2_out), .out(delay_3_out));
  Delay #(.delayTime(5)) delay_4 (.in(delay_3_out), .out(delay_4_out));
  Multiplexer multiplexer_19 (
    .sel(pulldown_43_out[2]), .in_0(delay_4_out), .in_1(multiplexer_26_out), .out(multiplexer_19_out));
  Multiplexer multiplexer_20 (
    .sel(pulldown_43_out[2]), .in_0(delay_4_out), .in_1(multiplexer_27_out), .out(multiplexer_20_out));
  Multiplexer multiplexer_21 (
    .sel(pulldown_43_out[2]), .in_0(delay_4_out), .in_1(multiplexer_28_out), .out(multiplexer_21_out));
  Multiplexer multiplexer_22 (
    .sel(pulldown_43_out[2]), .in_0(delay_4_out), .in_1(multiplexer_29_out), .out(multiplexer_22_out));
  Multiplexer multiplexer_23 (
    .sel(pulldown_43_out[2]), .in_0(delay_4_out), .in_1(multiplexer_30_out), .out(multiplexer_23_out));
  Multiplexer multiplexer_24 (
    .sel(pulldown_43_out[2]), .in_0(delay_4_out), .in_1(multiplexer_31_out), .out(multiplexer_24_out));
  Multiplexer multiplexer_25 (
    .sel(pulldown_43_out[2]), .in_0(delay_4_out), .in_1(multiplexer_32_out), .out(multiplexer_25_out));
  PullDown pulldown_9 (.out(pulldown_9_out));
  PullDown pulldown_10 (.out(pulldown_10_out));
  PullDown pulldown_11 (.out(pulldown_43_out[22]));
  PullDown pulldown_12 (.out(pulldown_43_out[21]));
  JK_FF jk_ff_1 (.J(multiplexer_9_out), .C(delay_4_out), .K(xor_1_out), .Q(jk_ff_5_q[0]), .nQ(jk_ff_1_nq));
  JK_FF jk_ff_2 (.J(multiplexer_10_out), .C(multiplexer_19_out), .K(xor_2_out), .Q(jk_ff_5_q[1]), .nQ(jk_ff_2_nq));
  JK_FF jk_ff_3 (.J(multiplexer_11_out), .C(multiplexer_20_out), .K(xor_3_out), .Q(jk_ff_5_q[2]), .nQ(jk_ff_3_nq));
  JK_FF jk_ff_4 (.J(multiplexer_12_out), .C(multiplexer_21_out), .K(xor_4_out), .Q(jk_ff_5_q[3]), .nQ(jk_ff_4_nq));
  JK_FF jk_ff_5 (.J(multiplexer_13_out), .C(multiplexer_22_out), .K(xor_5_out), .Q(jk_ff_5_q[4]), .nQ(jk_ff_5_nq));
  JK_FF jk_ff_6 (.J(multiplexer_14_out), .C(multiplexer_23_out), .K(xor_6_out), .Q(jk_ff_5_q[5]), .nQ(jk_ff_6_nq));
  JK_FF jk_ff_7 (.J(multiplexer_15_out), .C(multiplexer_24_out), .K(xor_7_out), .Q(jk_ff_5_q[6]), .nQ(jk_ff_7_nq));
  JK_FF jk_ff_8 (.J(multiplexer_16_out), .C(multiplexer_25_out), .K(xor_8_out), .Q(jk_ff_5_q[7]));  // open: nQ
  and and_8 (and_8_out, d_ff_5_q[0], and_10_out);
  and and_9 (and_9_out, and_8_out, d_ff_9_q);
  or or_3 (or_3_out, and_12_out, and_9_out);
  PullDown pulldown_13 (.out(pulldown_43_out[20]));
  PullDown pulldown_14 (.out(pulldown_43_out[19]));
  PullDown pulldown_15 (.out(pulldown_43_out[18]));
  PullDown pulldown_16 (.out(pulldown_43_out[17]));
  and and_10 (and_10_out, d_ff_5_q[1], d_ff_5_q[2], d_ff_5_q[3]);
  and and_11 (and_11_out, ~d_ff_5_q[0], and_10_out);  // And
  and and_12 (and_12_out, and_11_out, d_ff_10_q);
  PullDown pulldown_17 (.out(pulldown_43_out[16]));
  PullDown pulldown_18 (.out(pulldown_43_out[15]));
  PullDown pulldown_19 (.out(pulldown_43_out[14]));
  PullDown pulldown_20 (.out(pulldown_43_out[13]));
  Multiplexer multiplexer_26 (
    .sel(pulldown_43_out[1]), .in_0(jk_ff_1_nq), .in_1(jk_ff_5_q[0]), .out(multiplexer_26_out));
  Multiplexer multiplexer_27 (
    .sel(pulldown_43_out[1]), .in_0(jk_ff_2_nq), .in_1(jk_ff_5_q[1]), .out(multiplexer_27_out));
  Multiplexer multiplexer_28 (
    .sel(pulldown_43_out[1]), .in_0(jk_ff_3_nq), .in_1(jk_ff_5_q[2]), .out(multiplexer_28_out));
  Multiplexer multiplexer_29 (
    .sel(pulldown_43_out[1]), .in_0(jk_ff_4_nq), .in_1(jk_ff_5_q[3]), .out(multiplexer_29_out));
  Multiplexer multiplexer_30 (
    .sel(pulldown_43_out[1]), .in_0(jk_ff_5_nq), .in_1(jk_ff_5_q[4]), .out(multiplexer_30_out));
  Multiplexer multiplexer_31 (
    .sel(pulldown_43_out[1]), .in_0(jk_ff_6_nq), .in_1(jk_ff_5_q[5]), .out(multiplexer_31_out));
  Multiplexer multiplexer_32 (
    .sel(pulldown_43_out[1]), .in_0(jk_ff_7_nq), .in_1(jk_ff_5_q[6]), .out(multiplexer_32_out));
  PullDown pulldown_21 (.out(pulldown_43_out[23]));
  Multiplexer multiplexer_33 (.sel(and_6_out), .in_0(pulldown_43_out[23]), .in_1(and_6_out), .out(pulldown_10_out));
  PullDown pulldown_22 (.out(pulldown_43_out[3]));
  Multiplexer multiplexer_34 (.sel(and_6_out), .in_0(pulldown_43_out[3]), .in_1(and_6_out), .out(multiplexer_34_out));
  PullDown pulldown_23 (.out(pulldown_43_out[24]));
  Multiplexer multiplexer_35 (.sel(and_7_out), .in_0(pulldown_43_out[24]), .in_1(and_7_out), .out(pulldown_9_out));
  PullDown pulldown_24 (.out(pulldown_43_out[9]));
  Multiplexer multiplexer_36 (.sel(and_7_out), .in_0(pulldown_43_out[9]), .in_1(and_7_out), .out(multiplexer_36_out));
  or or_4 (or_4_out, and_7_out, and_6_out);
  PullDown pulldown_25 (.out(pulldown_43_out[12]));
  PullDown pulldown_26 (.out(pulldown_43_out[11]));
  PullDown pulldown_27 (.out(pulldown_27_out));
  PullDown pulldown_28 (.out(multiplexer_36_out));
  assign driver_8_out[7] = demultiplexer_3_out_3 ? jk_ff_5_q[0] : 1'bz;  // Driver driver_1
  assign driver_8_out[6] = demultiplexer_3_out_3 ? jk_ff_5_q[1] : 1'bz;  // Driver driver_2
  assign driver_8_out[5] = demultiplexer_3_out_3 ? jk_ff_5_q[2] : 1'bz;  // Driver driver_3
  assign driver_8_out[4] = demultiplexer_3_out_3 ? jk_ff_5_q[3] : 1'bz;  // Driver driver_4
  assign driver_8_out[3] = demultiplexer_3_out_3 ? jk_ff_5_q[4] : 1'bz;  // Driver driver_5
  assign driver_8_out[2] = demultiplexer_3_out_3 ? jk_ff_5_q[5] : 1'bz;  // Driver driver_6
  assign driver_8_out[1] = demultiplexer_3_out_3 ? jk_ff_5_q[6] : 1'bz;  // Driver driver_7
  assign driver_8_out[0] = demultiplexer_3_out_3 ? jk_ff_5_q[7] : 1'bz;  // Driver driver_8
  Multiplexer multiplexer_37 (
    .sel(or_4_out), .in_0(pulldown_43_out[7]), .in_1(pulldown_30_out), .out(multiplexer_37_out));
  PullDown pulldown_29 (.out(pulldown_43_out[7]));
  PullDown pulldown_30 (.out(pulldown_30_out));
  Multiplexer multiplexer_38 (
    .sel(or_4_out), .in_0(pulldown_43_out[8]), .in_1(pulldown_32_out), .out(multiplexer_38_out));
  PullDown pulldown_31 (.out(pulldown_43_out[8]));
  PullDown pulldown_32 (.out(pulldown_32_out));
  Multiplexer multiplexer_39 (
    .sel(or_4_out), .in_0(pulldown_43_out[10]), .in_1(pulldown_34_out), .out(pulldown_27_out));
  PullDown pulldown_33 (.out(pulldown_43_out[10]));
  PullDown pulldown_34 (.out(pulldown_34_out));
  PullDown pulldown_35 (.out(multiplexer_38_out));
  PullDown pulldown_36 (.out(multiplexer_37_out));
  PullDown pulldown_37 (.out(pulldown_43_out[6]));
  PullDown pulldown_38 (.out(pulldown_43_out[5]));
  RAMDualPort #(.AddrBits(8), .isProgramMemory("true"), .Bits(8)) ramdualport_1 (
    .A(jk_ff_5_q), .Din(driver_11_out), .str(pulldown_43_out[6]), .C(CLK), .ld(demultiplexer_3_out_2),
    .D(ramdualport_1_d));
  Multiplexer multiplexer_40 (
    .sel(multiplexer_48_out), .in_0(d_ff_1_q), .in_1(ramdualport_1_d[0]), .out(multiplexer_40_out));
  Multiplexer multiplexer_41 (
    .sel(multiplexer_48_out), .in_0(d_ff_2_q), .in_1(ramdualport_1_d[1]), .out(multiplexer_41_out));
  Multiplexer multiplexer_42 (
    .sel(multiplexer_48_out), .in_0(d_ff_3_q), .in_1(ramdualport_1_d[2]), .out(multiplexer_42_out));
  Multiplexer multiplexer_43 (
    .sel(multiplexer_48_out), .in_0(d_ff_4_q), .in_1(ramdualport_1_d[3]), .out(multiplexer_43_out));
  Multiplexer multiplexer_44 (
    .sel(multiplexer_48_out), .in_0(d_ff_5_q[0]), .in_1(ramdualport_1_d[4]), .out(multiplexer_44_out));
  Multiplexer multiplexer_45 (
    .sel(multiplexer_48_out), .in_0(d_ff_5_q[1]), .in_1(ramdualport_1_d[5]), .out(multiplexer_45_out));
  Multiplexer multiplexer_46 (
    .sel(multiplexer_48_out), .in_0(d_ff_5_q[2]), .in_1(ramdualport_1_d[6]), .out(multiplexer_46_out));
  Multiplexer multiplexer_47 (
    .sel(multiplexer_48_out), .in_0(d_ff_5_q[3]), .in_1(ramdualport_1_d[7]), .out(multiplexer_47_out));
  PullDown pulldown_39 (.out(pulldown_43_out[4]));
  PullDown pulldown_40 (.out(multiplexer_34_out));
  PullDown pulldown_41 (.out(pulldown_43_out[2]));
  PullDown pulldown_42 (.out(pulldown_43_out[1]));
  D_FF d_ff_1 (.D(multiplexer_40_out), .C(CLK), .Q(d_ff_1_q));  // open: nQ
  D_FF d_ff_2 (.D(multiplexer_41_out), .C(CLK), .Q(d_ff_2_q));  // open: nQ
  D_FF d_ff_3 (.D(multiplexer_42_out), .C(CLK), .Q(d_ff_3_q));  // open: nQ
  D_FF d_ff_4 (.D(multiplexer_43_out), .C(CLK), .Q(d_ff_4_q));  // open: nQ
  D_FF d_ff_5 (.D(multiplexer_44_out), .C(CLK), .Q(d_ff_5_q[0]));  // open: nQ
  D_FF d_ff_6 (.D(multiplexer_45_out), .C(CLK), .Q(d_ff_5_q[1]));  // open: nQ
  D_FF d_ff_7 (.D(multiplexer_46_out), .C(CLK), .Q(d_ff_5_q[2]));  // open: nQ
  D_FF d_ff_8 (.D(multiplexer_47_out), .C(CLK), .Q(d_ff_5_q[3]));  // open: nQ
  Multiplexer multiplexer_48 (.sel(and_4_out), .in_0(pulldown_43_out[0]), .in_1(and_4_out), .out(multiplexer_48_out));
  PullDown pulldown_43 (.out(pulldown_43_out[0]));
  LED led_1 (.in(jk_ff_5_q[7]));
  LED led_2 (.in(d_ff_5_q[3]));
  ROM #(.AddrBits(5), .Bits(32)) rom_1 (.A(d_ff_5_q), .sel(not_4_out), .D({out_42, pulldown_43_out}));
  LED led_3 (.in(jk_ff_5_q[5]));
  LED led_4 (.in(jk_ff_5_q[6]));
  LED led_5 (.in(d_ff_5_q[2]));
  LED led_6 (.in(d_ff_5_q[1]));
  or or_5 (or_5_out, multiplexer_34_out, and_5_out, and_4_out);
  LED led_7 (.in(jk_ff_5_q[4]));
  LED led_8 (.in(jk_ff_5_q[3]));
  LED led_9 (.in(d_ff_5_q[0]));
  LED led_10 (.in(d_ff_4_q));
  LED led_11 (.in(jk_ff_5_q[2]));
  LED led_12 (.in(jk_ff_5_q[1]));
  assign driver_11_out[7] = pulldown_43_out[6] ? ramdualport_1_d[7] : 1'bz;  // Driver driver_9
  assign driver_11_out[6] = pulldown_43_out[6] ? ramdualport_1_d[6] : 1'bz;  // Driver driver_10
  assign driver_11_out[5] = pulldown_43_out[6] ? ramdualport_1_d[5] : 1'bz;  // Driver driver_11
  assign driver_11_out[4] = pulldown_43_out[6] ? ramdualport_1_d[4] : 1'bz;  // Driver driver_12
  assign driver_11_out[3] = pulldown_43_out[6] ? ramdualport_1_d[3] : 1'bz;  // Driver driver_13
  assign driver_11_out[2] = pulldown_43_out[6] ? ramdualport_1_d[2] : 1'bz;  // Driver driver_14
  assign driver_11_out[1] = pulldown_43_out[6] ? ramdualport_1_d[1] : 1'bz;  // Driver driver_15
  assign driver_11_out[0] = pulldown_43_out[6] ? ramdualport_1_d[0] : 1'bz;  // Driver driver_16
  LED led_13 (.in(d_ff_2_q));
  LED led_14 (.in(d_ff_3_q));
  Multiplexer multiplexer_49 (.sel(or_6_out), .in_0(multiplexer_37_out), .in_1(or_6_out), .out(multiplexer_49_out));
  LED led_15 (.in(jk_ff_5_q[0]));
  Demultiplexer #(.Bits(8)) demultiplexer_1 (
    .sel(delay_6_out), .in(driver_8_out), .out_0(demultiplexer_1_out_0), .out_1(demultiplexer_1_out_1));
  LED led_16 (.in(d_ff_1_q));
  assign ramdualport_1_d[0] = demultiplexer_3_out_1 ? d_ff_1_q : 1'bz;  // Driver driver_17
  assign ramdualport_1_d[1] = demultiplexer_3_out_1 ? d_ff_2_q : 1'bz;  // Driver driver_18
  assign ramdualport_1_d[2] = demultiplexer_3_out_1 ? d_ff_3_q : 1'bz;  // Driver driver_19
  assign ramdualport_1_d[3] = demultiplexer_3_out_1 ? d_ff_4_q : 1'bz;  // Driver driver_20
  assign ramdualport_1_d[4] = demultiplexer_3_out_1 ? 1'b0 : 1'bz;  // Driver driver_21
  assign ramdualport_1_d[5] = demultiplexer_3_out_1 ? 1'b0 : 1'bz;  // Driver driver_22
  assign ramdualport_1_d[6] = demultiplexer_3_out_1 ? 1'b0 : 1'bz;  // Driver driver_23
  assign ramdualport_1_d[7] = demultiplexer_3_out_1 ? 1'b0 : 1'bz;  // Driver driver_24
  Multiplexer multiplexer_50 (.sel(or_6_out), .in_0(multiplexer_38_out), .in_1(or_6_out), .out(multiplexer_50_out));
  and and_13 (and_13_out, demultiplexer_3_out_3, ~pulldown_43_out[30]);  // And
  Delay #(.delayTime(2)) delay_5 (.in(pulldown_43_out[30]), .out(delay_5_out));
  Delay delay_6 (.in(delay_5_out), .out(delay_6_out));
  Multiplexer multiplexer_51 (.sel(and_4_out), .in_0(multiplexer_36_out), .in_1(and_4_out), .out(multiplexer_51_out));
  Multiplexer multiplexer_52 (.sel(or_6_out), .in_0(pulldown_27_out), .in_1(or_6_out), .out(multiplexer_52_out));
  assign {ramdualport_1_d[0], ramdualport_1_d[1], ramdualport_1_d[2], ramdualport_1_d[3], ramdualport_1_d[4], ramdualport_1_d[5], ramdualport_1_d[6], ramdualport_1_d[7]} = and_13_out ? demultiplexer_1_out_0 : 8'bz;  // Driver driver_25
  Multiplexer #(.Bits(8)) multiplexer_53 (
    .sel(delay_5_out),
    .in_0({ramdualport_1_d[0], ramdualport_1_d[1], ramdualport_1_d[2], ramdualport_1_d[3], ramdualport_1_d[4], ramdualport_1_d[5], ramdualport_1_d[6], ramdualport_1_d[7]}),
    .in_1(demultiplexer_2_out_1), .out(multiplexer_53_out));
  or or_6 (or_6_out, and_5_out, and_4_out);
  LED led_17 (.in(ramdualport_1_d[6]));
  LED led_18 (.in(ramdualport_1_d[7]));
  LED led_19 (.in(ramdualport_1_d[4]));
  LED led_20 (.in(ramdualport_1_d[5]));
  LED led_21 (.in(ramdualport_1_d[3]));
  LED led_22 (.in(ramdualport_1_d[2]));
  LED led_23 (.in(ramdualport_1_d[1]));
  LED led_24 (.in(ramdualport_1_d[0]));
  assign {ramdualport_1_d[0], ramdualport_1_d[1], ramdualport_1_d[2], ramdualport_1_d[3], ramdualport_1_d[4], ramdualport_1_d[5], ramdualport_1_d[6], ramdualport_1_d[7]} = and_14_out ? demultiplexer_2_out_0 : 8'bz;  // Driver driver_26
  Demultiplexer #(.Bits(8)) demultiplexer_2 (
    .sel(delay_8_out), .in(driver_66_out), .out_0(demultiplexer_2_out_0), .out_1(demultiplexer_2_out_1));
  assign ramdualport_1_d[7] = EN ? D7 : 1'bz;  // Driver driver_27
  Delay #(.delayTime(2)) delay_7 (.in(pulldown_43_out[30]), .out(delay_7_out));
  Delay delay_8 (.in(delay_7_out), .out(delay_8_out));
  assign ramdualport_1_d[6] = EN ? D6 : 1'bz;  // Driver driver_28
  assign ramdualport_1_d[5] = EN ? D5 : 1'bz;  // Driver driver_29
  and and_14 (and_14_out, ~pulldown_43_out[30], multiplexer_18_out);  // And
  Multiplexer #(.Bits(8)) multiplexer_54 (
    .sel(delay_7_out),
    .in_0({ramdualport_1_d[0], ramdualport_1_d[1], ramdualport_1_d[2], ramdualport_1_d[3], ramdualport_1_d[4], ramdualport_1_d[5], ramdualport_1_d[6], ramdualport_1_d[7]}),
    .in_1(demultiplexer_1_out_1), .out(multiplexer_54_out));
  assign ramdualport_1_d[4] = EN ? D4 : 1'bz;  // Driver driver_30
  assign ramdualport_1_d[3] = EN ? D3 : 1'bz;  // Driver driver_31
  Multiplexer multiplexer_55 (
    .sel(multiplexer_159_out), .in_0(ramdualport_1_d[0]), .in_1(multiplexer_157_out), .out(multiplexer_55_out));
  Multiplexer multiplexer_56 (
    .sel(multiplexer_159_out), .in_0(ramdualport_1_d[1]), .in_1(multiplexer_157_out), .out(multiplexer_56_out));
  Multiplexer multiplexer_57 (
    .sel(multiplexer_159_out), .in_0(ramdualport_1_d[2]), .in_1(multiplexer_157_out), .out(multiplexer_57_out));
  Multiplexer multiplexer_58 (
    .sel(multiplexer_159_out), .in_0(ramdualport_1_d[3]), .in_1(multiplexer_157_out), .out(multiplexer_58_out));
  Multiplexer multiplexer_59 (
    .sel(multiplexer_159_out), .in_0(ramdualport_1_d[4]), .in_1(multiplexer_157_out), .out(multiplexer_59_out));
  Multiplexer multiplexer_60 (
    .sel(multiplexer_159_out), .in_0(ramdualport_1_d[5]), .in_1(multiplexer_157_out), .out(multiplexer_60_out));
  Multiplexer multiplexer_61 (
    .sel(multiplexer_159_out), .in_0(ramdualport_1_d[6]), .in_1(multiplexer_157_out), .out(multiplexer_61_out));
  Multiplexer multiplexer_62 (
    .sel(multiplexer_159_out), .in_0(ramdualport_1_d[7]), .in_1(multiplexer_157_out), .out(multiplexer_62_out));
  and and_15 (and_15_out, jk_ff_17_q, jk_ff_9_q);
  and and_16 (and_16_out, jk_ff_18_q, jk_ff_10_q);
  and and_17 (and_17_out, jk_ff_19_q, jk_ff_11_q);
  and and_18 (and_18_out, jk_ff_20_q, jk_ff_12_q);
  and and_19 (and_19_out, jk_ff_21_q, jk_ff_13_q);
  and and_20 (and_20_out, jk_ff_22_q, jk_ff_14_q);
  and and_21 (and_21_out, jk_ff_23_q, jk_ff_15_q);
  and and_22 (and_22_out, jk_ff_24_q, jk_ff_16_q);
  Multiplexer multiplexer_63 (
    .sel(multiplexer_156_out), .in_0(ramdualport_1_d[0]), .in_1(multiplexer_155_out), .out(multiplexer_63_out));
  Multiplexer multiplexer_64 (
    .sel(multiplexer_156_out), .in_0(ramdualport_1_d[1]), .in_1(multiplexer_155_out), .out(multiplexer_64_out));
  Multiplexer multiplexer_65 (
    .sel(multiplexer_156_out), .in_0(ramdualport_1_d[2]), .in_1(multiplexer_155_out), .out(multiplexer_65_out));
  Multiplexer multiplexer_66 (
    .sel(multiplexer_156_out), .in_0(ramdualport_1_d[3]), .in_1(multiplexer_155_out), .out(multiplexer_66_out));
  Multiplexer multiplexer_67 (
    .sel(multiplexer_156_out), .in_0(ramdualport_1_d[4]), .in_1(multiplexer_155_out), .out(multiplexer_67_out));
  Multiplexer multiplexer_68 (
    .sel(multiplexer_156_out), .in_0(ramdualport_1_d[5]), .in_1(multiplexer_155_out), .out(multiplexer_68_out));
  Multiplexer multiplexer_69 (
    .sel(multiplexer_156_out), .in_0(ramdualport_1_d[6]), .in_1(multiplexer_155_out), .out(multiplexer_69_out));
  Multiplexer multiplexer_70 (
    .sel(multiplexer_156_out), .in_0(ramdualport_1_d[7]), .in_1(multiplexer_155_out), .out(multiplexer_70_out));
  assign ramdualport_1_d[2] = EN ? D2 : 1'bz;  // Driver driver_32
  assign ramdualport_1_d[1] = EN ? D1 : 1'bz;  // Driver driver_33
  and and_23 (and_23_out, multiplexer_163_out, multiplexer_165_out);
  not not_7 (not_7_out, and_23_out);
  and and_24 (and_24_out, multiplexer_158_out, multiplexer_162_out);
  not not_8 (not_8_out, and_24_out);
  assign ramdualport_1_d[0] = EN ? D0 : 1'bz;  // Driver driver_34
  Multiplexer multiplexer_71 (
    .sel(multiplexer_49_out), .in_0(multiplexer_54_out[7]), .in_1(1'b1), .out(multiplexer_71_out));
  Multiplexer multiplexer_72 (
    .sel(multiplexer_49_out), .in_0(multiplexer_54_out[6]), .in_1(1'b1), .out(multiplexer_72_out));
  Multiplexer multiplexer_73 (
    .sel(multiplexer_49_out), .in_0(multiplexer_54_out[5]), .in_1(1'b1), .out(multiplexer_73_out));
  Multiplexer multiplexer_74 (
    .sel(multiplexer_49_out), .in_0(multiplexer_54_out[4]), .in_1(1'b1), .out(multiplexer_74_out));
  Multiplexer multiplexer_75 (
    .sel(multiplexer_49_out), .in_0(multiplexer_54_out[3]), .in_1(1'b1), .out(multiplexer_75_out));
  Multiplexer multiplexer_76 (
    .sel(multiplexer_49_out), .in_0(multiplexer_54_out[2]), .in_1(1'b1), .out(multiplexer_76_out));
  Multiplexer multiplexer_77 (
    .sel(multiplexer_49_out), .in_0(multiplexer_54_out[1]), .in_1(1'b1), .out(multiplexer_77_out));
  Multiplexer multiplexer_78 (
    .sel(multiplexer_49_out), .in_0(multiplexer_54_out[0]), .in_1(1'b1), .out(multiplexer_78_out));
  Multiplexer multiplexer_79 (
    .sel(multiplexer_165_out), .in_0(jk_ff_9_q), .in_1(multiplexer_55_out), .out(multiplexer_79_out));
  Multiplexer multiplexer_80 (
    .sel(multiplexer_165_out), .in_0(jk_ff_10_q), .in_1(multiplexer_56_out), .out(multiplexer_80_out));
  Multiplexer multiplexer_81 (
    .sel(multiplexer_165_out), .in_0(jk_ff_11_q), .in_1(multiplexer_57_out), .out(multiplexer_81_out));
  Multiplexer multiplexer_82 (
    .sel(multiplexer_165_out), .in_0(jk_ff_12_q), .in_1(multiplexer_58_out), .out(multiplexer_82_out));
  Multiplexer multiplexer_83 (
    .sel(multiplexer_165_out), .in_0(jk_ff_13_q), .in_1(multiplexer_59_out), .out(multiplexer_83_out));
  Multiplexer multiplexer_84 (
    .sel(multiplexer_165_out), .in_0(jk_ff_14_q), .in_1(multiplexer_60_out), .out(multiplexer_84_out));
  Multiplexer multiplexer_85 (
    .sel(multiplexer_165_out), .in_0(jk_ff_15_q), .in_1(multiplexer_61_out), .out(multiplexer_85_out));
  Multiplexer multiplexer_86 (
    .sel(multiplexer_165_out), .in_0(jk_ff_16_q), .in_1(multiplexer_62_out), .out(multiplexer_86_out));
  Multiplexer multiplexer_87 (
    .sel(multiplexer_162_out), .in_0(jk_ff_17_q), .in_1(multiplexer_63_out), .out(multiplexer_87_out));
  Multiplexer multiplexer_88 (
    .sel(multiplexer_162_out), .in_0(jk_ff_18_q), .in_1(multiplexer_64_out), .out(multiplexer_88_out));
  Multiplexer multiplexer_89 (
    .sel(multiplexer_162_out), .in_0(jk_ff_19_q), .in_1(multiplexer_65_out), .out(multiplexer_89_out));
  Multiplexer multiplexer_90 (
    .sel(multiplexer_162_out), .in_0(jk_ff_20_q), .in_1(multiplexer_66_out), .out(multiplexer_90_out));
  Multiplexer multiplexer_91 (
    .sel(multiplexer_162_out), .in_0(jk_ff_21_q), .in_1(multiplexer_67_out), .out(multiplexer_91_out));
  Multiplexer multiplexer_92 (
    .sel(multiplexer_162_out), .in_0(jk_ff_22_q), .in_1(multiplexer_68_out), .out(multiplexer_92_out));
  Multiplexer multiplexer_93 (
    .sel(multiplexer_162_out), .in_0(jk_ff_23_q), .in_1(multiplexer_69_out), .out(multiplexer_93_out));
  Multiplexer multiplexer_94 (
    .sel(multiplexer_162_out), .in_0(jk_ff_24_q), .in_1(multiplexer_70_out), .out(multiplexer_94_out));
  and and_25 (and_25_out, multiplexer_50_out, multiplexer_51_out);
  not not_9 (not_9_out, and_25_out);
  xor xor_9 (xor_9_out, multiplexer_79_out, not_7_out);
  xor xor_10 (xor_10_out, multiplexer_80_out, not_7_out);
  xor xor_11 (xor_11_out, multiplexer_81_out, not_7_out);
  xor xor_12 (xor_12_out, multiplexer_82_out, not_7_out);
  xor xor_13 (xor_13_out, multiplexer_83_out, not_7_out);
  xor xor_14 (xor_14_out, multiplexer_84_out, not_7_out);
  xor xor_15 (xor_15_out, multiplexer_85_out, not_7_out);
  xor xor_16 (xor_16_out, multiplexer_86_out, not_7_out);
  xor xor_17 (xor_17_out, multiplexer_87_out, not_8_out);
  xor xor_18 (xor_18_out, multiplexer_88_out, not_8_out);
  xor xor_19 (xor_19_out, multiplexer_89_out, not_8_out);
  xor xor_20 (xor_20_out, multiplexer_90_out, not_8_out);
  xor xor_21 (xor_21_out, multiplexer_91_out, not_8_out);
  xor xor_22 (xor_22_out, multiplexer_92_out, not_8_out);
  xor xor_23 (xor_23_out, multiplexer_93_out, not_8_out);
  xor xor_24 (xor_24_out, multiplexer_94_out, not_8_out);
  Multiplexer multiplexer_95 (.sel(and_5_out), .in_0(pulldown_10_out), .in_1(and_5_out), .out(multiplexer_95_out[2]));
  Multiplexer multiplexer_96 (
    .sel(multiplexer_51_out), .in_0(jk_ff_25_q), .in_1(multiplexer_71_out), .out(multiplexer_96_out));
  Multiplexer multiplexer_97 (
    .sel(multiplexer_51_out), .in_0(jk_ff_26_q), .in_1(multiplexer_72_out), .out(multiplexer_97_out));
  Multiplexer multiplexer_98 (
    .sel(multiplexer_51_out), .in_0(jk_ff_27_q), .in_1(multiplexer_73_out), .out(multiplexer_98_out));
  Multiplexer multiplexer_99 (
    .sel(multiplexer_51_out), .in_0(jk_ff_28_q), .in_1(multiplexer_74_out), .out(multiplexer_99_out));
  Multiplexer multiplexer_100 (
    .sel(multiplexer_51_out), .in_0(jk_ff_29_q), .in_1(multiplexer_75_out), .out(multiplexer_100_out));
  Multiplexer multiplexer_101 (
    .sel(multiplexer_51_out), .in_0(jk_ff_30_q), .in_1(multiplexer_76_out), .out(multiplexer_101_out));
  Multiplexer multiplexer_102 (
    .sel(multiplexer_51_out), .in_0(jk_ff_31_q), .in_1(multiplexer_77_out), .out(multiplexer_102_out));
  Multiplexer multiplexer_103 (
    .sel(multiplexer_51_out), .in_0(jk_ff_32_q), .in_1(multiplexer_78_out), .out(multiplexer_103_out));
  Multiplexer multiplexer_104 (.sel(and_4_out), .in_0(pulldown_9_out), .in_1(and_4_out), .out(multiplexer_95_out[1]));
  xor xor_25 (xor_25_out, multiplexer_96_out, not_9_out);
  xor xor_26 (xor_26_out, multiplexer_97_out, not_9_out);
  xor xor_27 (xor_27_out, multiplexer_98_out, not_9_out);
  xor xor_28 (xor_28_out, multiplexer_99_out, not_9_out);
  xor xor_29 (xor_29_out, multiplexer_100_out, not_9_out);
  xor xor_30 (xor_30_out, multiplexer_101_out, not_9_out);
  xor xor_31 (xor_31_out, multiplexer_102_out, not_9_out);
  xor xor_32 (xor_32_out, multiplexer_103_out, not_9_out);
  Multiplexer multiplexer_105 (
    .sel(multiplexer_167_out), .in_0(CLK), .in_1(multiplexer_134_out), .out(multiplexer_105_out));
  Multiplexer multiplexer_106 (
    .sel(multiplexer_167_out), .in_0(CLK), .in_1(multiplexer_135_out), .out(multiplexer_106_out));
  Multiplexer multiplexer_107 (
    .sel(multiplexer_167_out), .in_0(CLK), .in_1(multiplexer_136_out), .out(multiplexer_107_out));
  Multiplexer multiplexer_108 (
    .sel(multiplexer_167_out), .in_0(CLK), .in_1(multiplexer_137_out), .out(multiplexer_108_out));
  Multiplexer multiplexer_109 (
    .sel(multiplexer_167_out), .in_0(CLK), .in_1(multiplexer_138_out), .out(multiplexer_109_out));
  Multiplexer multiplexer_110 (
    .sel(multiplexer_167_out), .in_0(CLK), .in_1(multiplexer_139_out), .out(multiplexer_110_out));
  Multiplexer multiplexer_111 (
    .sel(multiplexer_167_out), .in_0(CLK), .in_1(multiplexer_140_out), .out(multiplexer_111_out));
  Add add_1 (.a(jk_ff_9_q), .b(jk_ff_17_q), .c_i(pulldown_43_out[17]), .s(add_1_s), .c_o(add_1_c_o));
  Add add_2 (.a(jk_ff_11_q), .b(jk_ff_19_q), .c_i(add_5_c_o), .s(add_2_s), .c_o(add_2_c_o));
  Add add_3 (.a(jk_ff_13_q), .b(jk_ff_21_q), .c_i(add_6_c_o), .s(add_3_s), .c_o(add_3_c_o));
  Add add_4 (.a(jk_ff_15_q), .b(jk_ff_23_q), .c_i(add_7_c_o), .s(add_4_s), .c_o(add_4_c_o));
  Multiplexer multiplexer_112 (
    .sel(multiplexer_164_out), .in_0(CLK), .in_1(multiplexer_141_out), .out(multiplexer_112_out));
  Multiplexer multiplexer_113 (
    .sel(multiplexer_164_out), .in_0(CLK), .in_1(multiplexer_142_out), .out(multiplexer_113_out));
  Multiplexer multiplexer_114 (
    .sel(multiplexer_164_out), .in_0(CLK), .in_1(multiplexer_143_out), .out(multiplexer_114_out));
  Multiplexer multiplexer_115 (
    .sel(multiplexer_164_out), .in_0(CLK), .in_1(multiplexer_144_out), .out(multiplexer_115_out));
  Multiplexer multiplexer_116 (
    .sel(multiplexer_164_out), .in_0(CLK), .in_1(multiplexer_145_out), .out(multiplexer_116_out));
  Multiplexer multiplexer_117 (
    .sel(multiplexer_164_out), .in_0(CLK), .in_1(multiplexer_146_out), .out(multiplexer_117_out));
  Multiplexer multiplexer_118 (
    .sel(multiplexer_164_out), .in_0(CLK), .in_1(multiplexer_147_out), .out(multiplexer_118_out));
  JK_FF jk_ff_9 (.J(multiplexer_79_out), .C(CLK), .K(xor_9_out), .Q(jk_ff_9_q), .nQ(jk_ff_9_nq));
  JK_FF jk_ff_10 (.J(multiplexer_80_out), .C(multiplexer_105_out), .K(xor_10_out), .Q(jk_ff_10_q), .nQ(jk_ff_10_nq));
  JK_FF jk_ff_11 (.J(multiplexer_81_out), .C(multiplexer_106_out), .K(xor_11_out), .Q(jk_ff_11_q), .nQ(jk_ff_11_nq));
  JK_FF jk_ff_12 (.J(multiplexer_82_out), .C(multiplexer_107_out), .K(xor_12_out), .Q(jk_ff_12_q), .nQ(jk_ff_12_nq));
  JK_FF jk_ff_13 (.J(multiplexer_83_out), .C(multiplexer_108_out), .K(xor_13_out), .Q(jk_ff_13_q), .nQ(jk_ff_13_nq));
  JK_FF jk_ff_14 (.J(multiplexer_84_out), .C(multiplexer_109_out), .K(xor_14_out), .Q(jk_ff_14_q), .nQ(jk_ff_14_nq));
  JK_FF jk_ff_15 (.J(multiplexer_85_out), .C(multiplexer_110_out), .K(xor_15_out), .Q(jk_ff_15_q), .nQ(jk_ff_15_nq));
  JK_FF jk_ff_16 (.J(multiplexer_86_out), .C(multiplexer_111_out), .K(xor_16_out), .Q(jk_ff_16_q));  // open: nQ
  Add add_5 (.a(jk_ff_10_q), .b(jk_ff_18_q), .c_i(add_1_c_o), .s(add_5_s), .c_o(add_5_c_o));
  Add add_6 (.a(jk_ff_12_q), .b(jk_ff_20_q), .c_i(add_2_c_o), .s(add_6_s), .c_o(add_6_c_o));
  Add add_7 (.a(jk_ff_14_q), .b(jk_ff_22_q), .c_i(add_3_c_o), .s(add_7_s), .c_o(add_7_c_o));
  Add add_8 (.a(jk_ff_16_q), .b(jk_ff_24_q), .c_i(add_4_c_o), .s(add_8_s), .c_o(add_8_c_o));
  JK_FF jk_ff_17 (.J(multiplexer_87_out), .C(CLK), .K(xor_17_out), .Q(jk_ff_17_q), .nQ(jk_ff_17_nq));
  JK_FF jk_ff_18 (.J(multiplexer_88_out), .C(multiplexer_112_out), .K(xor_18_out), .Q(jk_ff_18_q), .nQ(jk_ff_18_nq));
  JK_FF jk_ff_19 (.J(multiplexer_89_out), .C(multiplexer_113_out), .K(xor_19_out), .Q(jk_ff_19_q), .nQ(jk_ff_19_nq));
  JK_FF jk_ff_20 (.J(multiplexer_90_out), .C(multiplexer_114_out), .K(xor_20_out), .Q(jk_ff_20_q), .nQ(jk_ff_20_nq));
  JK_FF jk_ff_21 (.J(multiplexer_91_out), .C(multiplexer_115_out), .K(xor_21_out), .Q(jk_ff_21_q), .nQ(jk_ff_21_nq));
  JK_FF jk_ff_22 (.J(multiplexer_92_out), .C(multiplexer_116_out), .K(xor_22_out), .Q(jk_ff_22_q), .nQ(jk_ff_22_nq));
  JK_FF jk_ff_23 (.J(multiplexer_93_out), .C(multiplexer_117_out), .K(xor_23_out), .Q(jk_ff_23_q), .nQ(jk_ff_23_nq));
  JK_FF jk_ff_24 (.J(multiplexer_94_out), .C(multiplexer_118_out), .K(xor_24_out), .Q(jk_ff_24_q));  // open: nQ
  Demultiplexer #(.Selector_Bits(3)) demultiplexer_3 (
    .sel({multiplexer_95_out, pulldown_43_out[25]}), .in(1'b1), .out_1(demultiplexer_3_out_1),
    .out_2(demultiplexer_3_out_2), .out_3(demultiplexer_3_out_3), .out_4(pulldown_2_out),
    .out_5(demultiplexer_3_out_5), .out_6(demultiplexer_3_out_6), .out_7(demultiplexer_3_out_7));  // open: out_0
  Multiplexer multiplexer_119 (
    .sel(multiplexer_52_out), .in_0(CLK), .in_1(multiplexer_148_out), .out(multiplexer_119_out));
  Multiplexer multiplexer_120 (
    .sel(multiplexer_52_out), .in_0(CLK), .in_1(multiplexer_149_out), .out(multiplexer_120_out));
  Multiplexer multiplexer_121 (
    .sel(multiplexer_52_out), .in_0(CLK), .in_1(multiplexer_150_out), .out(multiplexer_121_out));
  Multiplexer multiplexer_122 (
    .sel(multiplexer_52_out), .in_0(CLK), .in_1(multiplexer_151_out), .out(multiplexer_122_out));
  Multiplexer multiplexer_123 (
    .sel(multiplexer_52_out), .in_0(CLK), .in_1(multiplexer_152_out), .out(multiplexer_123_out));
  Multiplexer multiplexer_124 (
    .sel(multiplexer_52_out), .in_0(CLK), .in_1(multiplexer_153_out), .out(multiplexer_124_out));
  Multiplexer multiplexer_125 (
    .sel(multiplexer_52_out), .in_0(CLK), .in_1(multiplexer_154_out), .out(multiplexer_125_out));
  Multiplexer multiplexer_126 (.sel(pulldown_43_out[29]), .in_0(add_1_s), .in_1(and_15_out), .out(multiplexer_126_out));
  Multiplexer multiplexer_127 (.sel(pulldown_43_out[29]), .in_0(add_5_s), .in_1(and_16_out), .out(multiplexer_127_out));
  Multiplexer multiplexer_128 (.sel(pulldown_43_out[29]), .in_0(add_2_s), .in_1(and_17_out), .out(multiplexer_128_out));
  Multiplexer multiplexer_129 (.sel(pulldown_43_out[29]), .in_0(add_6_s), .in_1(and_18_out), .out(multiplexer_129_out));
  Multiplexer multiplexer_130 (.sel(pulldown_43_out[29]), .in_0(add_3_s), .in_1(and_19_out), .out(multiplexer_130_out));
  Multiplexer multiplexer_131 (.sel(pulldown_43_out[29]), .in_0(add_7_s), .in_1(and_20_out), .out(multiplexer_131_out));
  Multiplexer multiplexer_132 (.sel(pulldown_43_out[29]), .in_0(add_4_s), .in_1(and_21_out), .out(multiplexer_132_out));
  Multiplexer multiplexer_133 (.sel(pulldown_43_out[29]), .in_0(add_8_s), .in_1(and_22_out), .out(multiplexer_133_out));
  JK_FF jk_ff_25 (.J(multiplexer_96_out), .C(CLK), .K(xor_25_out), .Q(jk_ff_25_q), .nQ(jk_ff_25_nq));
  JK_FF jk_ff_26 (.J(multiplexer_97_out), .C(multiplexer_119_out), .K(xor_26_out), .Q(jk_ff_26_q), .nQ(jk_ff_26_nq));
  JK_FF jk_ff_27 (.J(multiplexer_98_out), .C(multiplexer_120_out), .K(xor_27_out), .Q(jk_ff_27_q), .nQ(jk_ff_27_nq));
  JK_FF jk_ff_28 (.J(multiplexer_99_out), .C(multiplexer_121_out), .K(xor_28_out), .Q(jk_ff_28_q), .nQ(jk_ff_28_nq));
  JK_FF jk_ff_29 (.J(multiplexer_100_out), .C(multiplexer_122_out), .K(xor_29_out), .Q(jk_ff_29_q), .nQ(jk_ff_29_nq));
  JK_FF jk_ff_30 (.J(multiplexer_101_out), .C(multiplexer_123_out), .K(xor_30_out), .Q(jk_ff_30_q), .nQ(jk_ff_30_nq));
  JK_FF jk_ff_31 (.J(multiplexer_102_out), .C(multiplexer_124_out), .K(xor_31_out), .Q(jk_ff_31_q), .nQ(jk_ff_31_nq));
  JK_FF jk_ff_32 (.J(multiplexer_103_out), .C(multiplexer_125_out), .K(xor_32_out), .Q(jk_ff_32_q));  // open: nQ
  Multiplexer multiplexer_134 (
    .sel(multiplexer_168_out), .in_0(jk_ff_9_nq), .in_1(jk_ff_9_q), .out(multiplexer_134_out));
  Multiplexer multiplexer_135 (
    .sel(multiplexer_168_out), .in_0(jk_ff_10_nq), .in_1(jk_ff_10_q), .out(multiplexer_135_out));
  Multiplexer multiplexer_136 (
    .sel(multiplexer_168_out), .in_0(jk_ff_11_nq), .in_1(jk_ff_11_q), .out(multiplexer_136_out));
  Multiplexer multiplexer_137 (
    .sel(multiplexer_168_out), .in_0(jk_ff_12_nq), .in_1(jk_ff_12_q), .out(multiplexer_137_out));
  Multiplexer multiplexer_138 (
    .sel(multiplexer_168_out), .in_0(jk_ff_13_nq), .in_1(jk_ff_13_q), .out(multiplexer_138_out));
  Multiplexer multiplexer_139 (
    .sel(multiplexer_168_out), .in_0(jk_ff_14_nq), .in_1(jk_ff_14_q), .out(multiplexer_139_out));
  Multiplexer multiplexer_140 (
    .sel(multiplexer_168_out), .in_0(jk_ff_15_nq), .in_1(jk_ff_15_q), .out(multiplexer_140_out));
  assign ramdualport_1_d[0] = demultiplexer_3_out_6 ? multiplexer_126_out : 1'bz;  // Driver driver_35
  assign ramdualport_1_d[1] = demultiplexer_3_out_6 ? multiplexer_127_out : 1'bz;  // Driver driver_36
  assign ramdualport_1_d[2] = demultiplexer_3_out_6 ? multiplexer_128_out : 1'bz;  // Driver driver_37
  assign ramdualport_1_d[3] = demultiplexer_3_out_6 ? multiplexer_129_out : 1'bz;  // Driver driver_38
  assign ramdualport_1_d[4] = demultiplexer_3_out_6 ? multiplexer_130_out : 1'bz;  // Driver driver_39
  assign ramdualport_1_d[5] = demultiplexer_3_out_6 ? multiplexer_131_out : 1'bz;  // Driver driver_40
  assign ramdualport_1_d[6] = demultiplexer_3_out_6 ? multiplexer_132_out : 1'bz;  // Driver driver_41
  assign ramdualport_1_d[7] = demultiplexer_3_out_6 ? multiplexer_133_out : 1'bz;  // Driver driver_42
  Multiplexer multiplexer_141 (
    .sel(multiplexer_166_out), .in_0(jk_ff_17_nq), .in_1(jk_ff_17_q), .out(multiplexer_141_out));
  Multiplexer multiplexer_142 (
    .sel(multiplexer_166_out), .in_0(jk_ff_18_nq), .in_1(jk_ff_18_q), .out(multiplexer_142_out));
  Multiplexer multiplexer_143 (
    .sel(multiplexer_166_out), .in_0(jk_ff_19_nq), .in_1(jk_ff_19_q), .out(multiplexer_143_out));
  Multiplexer multiplexer_144 (
    .sel(multiplexer_166_out), .in_0(jk_ff_20_nq), .in_1(jk_ff_20_q), .out(multiplexer_144_out));
  Multiplexer multiplexer_145 (
    .sel(multiplexer_166_out), .in_0(jk_ff_21_nq), .in_1(jk_ff_21_q), .out(multiplexer_145_out));
  Multiplexer multiplexer_146 (
    .sel(multiplexer_166_out), .in_0(jk_ff_22_nq), .in_1(jk_ff_22_q), .out(multiplexer_146_out));
  Multiplexer multiplexer_147 (
    .sel(multiplexer_166_out), .in_0(jk_ff_23_nq), .in_1(jk_ff_23_q), .out(multiplexer_147_out));
  assign ramdualport_1_d[0] = demultiplexer_3_out_5 ? jk_ff_9_q : 1'bz;  // Driver driver_43
  assign ramdualport_1_d[1] = demultiplexer_3_out_5 ? jk_ff_10_q : 1'bz;  // Driver driver_44
  assign ramdualport_1_d[2] = demultiplexer_3_out_5 ? jk_ff_11_q : 1'bz;  // Driver driver_45
  assign ramdualport_1_d[3] = demultiplexer_3_out_5 ? jk_ff_12_q : 1'bz;  // Driver driver_46
  assign ramdualport_1_d[4] = demultiplexer_3_out_5 ? jk_ff_13_q : 1'bz;  // Driver driver_47
  assign ramdualport_1_d[5] = demultiplexer_3_out_5 ? jk_ff_14_q : 1'bz;  // Driver driver_48
  assign ramdualport_1_d[6] = demultiplexer_3_out_5 ? jk_ff_15_q : 1'bz;  // Driver driver_49
  assign ramdualport_1_d[7] = demultiplexer_3_out_5 ? jk_ff_16_q : 1'bz;  // Driver driver_50
  assign ramdualport_1_d[0] = demultiplexer_3_out_7 ? jk_ff_17_q : 1'bz;  // Driver driver_51
  assign ramdualport_1_d[1] = demultiplexer_3_out_7 ? jk_ff_18_q : 1'bz;  // Driver driver_52
  assign ramdualport_1_d[2] = demultiplexer_3_out_7 ? jk_ff_19_q : 1'bz;  // Driver driver_53
  assign ramdualport_1_d[3] = demultiplexer_3_out_7 ? jk_ff_20_q : 1'bz;  // Driver driver_54
  assign ramdualport_1_d[4] = demultiplexer_3_out_7 ? jk_ff_21_q : 1'bz;  // Driver driver_55
  assign ramdualport_1_d[5] = demultiplexer_3_out_7 ? jk_ff_22_q : 1'bz;  // Driver driver_56
  assign ramdualport_1_d[6] = demultiplexer_3_out_7 ? jk_ff_23_q : 1'bz;  // Driver driver_57
  assign ramdualport_1_d[7] = demultiplexer_3_out_7 ? jk_ff_24_q : 1'bz;  // Driver driver_58
  Multiplexer multiplexer_148 (
    .sel(pulldown_43_out[11]), .in_0(jk_ff_25_nq), .in_1(jk_ff_25_q), .out(multiplexer_148_out));
  Multiplexer multiplexer_149 (
    .sel(pulldown_43_out[11]), .in_0(jk_ff_26_nq), .in_1(jk_ff_26_q), .out(multiplexer_149_out));
  Multiplexer multiplexer_150 (
    .sel(pulldown_43_out[11]), .in_0(jk_ff_27_nq), .in_1(jk_ff_27_q), .out(multiplexer_150_out));
  Multiplexer multiplexer_151 (
    .sel(pulldown_43_out[11]), .in_0(jk_ff_28_nq), .in_1(jk_ff_28_q), .out(multiplexer_151_out));
  Multiplexer multiplexer_152 (
    .sel(pulldown_43_out[11]), .in_0(jk_ff_29_nq), .in_1(jk_ff_29_q), .out(multiplexer_152_out));
  Multiplexer multiplexer_153 (
    .sel(pulldown_43_out[11]), .in_0(jk_ff_30_nq), .in_1(jk_ff_30_q), .out(multiplexer_153_out));
  Multiplexer multiplexer_154 (
    .sel(pulldown_43_out[11]), .in_0(jk_ff_31_nq), .in_1(jk_ff_31_q), .out(multiplexer_154_out));
  assign driver_66_out[7] = multiplexer_18_out ? jk_ff_25_q : 1'bz;  // Driver driver_59
  assign driver_66_out[6] = multiplexer_18_out ? jk_ff_26_q : 1'bz;  // Driver driver_60
  assign driver_66_out[5] = multiplexer_18_out ? jk_ff_27_q : 1'bz;  // Driver driver_61
  assign driver_66_out[4] = multiplexer_18_out ? jk_ff_28_q : 1'bz;  // Driver driver_62
  assign driver_66_out[3] = multiplexer_18_out ? jk_ff_29_q : 1'bz;  // Driver driver_63
  assign driver_66_out[2] = multiplexer_18_out ? jk_ff_30_q : 1'bz;  // Driver driver_64
  assign driver_66_out[1] = multiplexer_18_out ? jk_ff_31_q : 1'bz;  // Driver driver_65
  assign driver_66_out[0] = multiplexer_18_out ? jk_ff_32_q : 1'bz;  // Driver driver_66
  LED led_25 (.in(jk_ff_16_q));
  LED led_26 (.in(multiplexer_133_out));
  LED led_27 (.in(jk_ff_24_q));
  LED led_28 (.in(jk_ff_14_q));
  LED led_29 (.in(jk_ff_15_q));
  LED led_30 (.in(multiplexer_132_out));
  LED led_31 (.in(multiplexer_131_out));
  LED led_32 (.in(jk_ff_22_q));
  LED led_33 (.in(jk_ff_23_q));
  LED led_34 (.in(jk_ff_32_q));
  LED led_35 (.in(jk_ff_13_q));
  LED led_36 (.in(jk_ff_12_q));
  LED led_37 (.in(multiplexer_130_out));
  LED led_38 (.in(multiplexer_129_out));
  LED led_39 (.in(jk_ff_21_q));
  LED led_40 (.in(jk_ff_20_q));
  LED led_41 (.in(jk_ff_30_q));
  LED led_42 (.in(jk_ff_31_q));
  LED led_43 (.in(jk_ff_11_q));
  LED led_44 (.in(jk_ff_10_q));
  LED led_45 (.in(multiplexer_128_out));
  LED led_46 (.in(multiplexer_127_out));
  LED led_47 (.in(jk_ff_19_q));
  LED led_48 (.in(jk_ff_18_q));
  or or_7 (or_7_out, decoder_2_out_1, decoder_2_out_7);
  and and_26 (and_26_out, ~decoder_2_out_7, and_1_out);  // And
  LED led_49 (.in(jk_ff_29_q));
  LED led_50 (.in(jk_ff_28_q));
  LED led_51 (.in(jk_ff_9_q));
  LED led_52 (.in(multiplexer_126_out));
  LED led_53 (.in(jk_ff_17_q));
  Multiplexer multiplexer_155 (.sel(not_11_out), .in_0(and_27_out), .in_1(1'b1), .out(multiplexer_155_out));
  and and_27 (and_27_out, not_15_out, or_8_out);
  or or_8 (or_8_out, or_7_out, decoder_2_out_4, decoder_2_out_0, decoder_2_out_6, decoder_2_out_2);
  and and_28 (and_28_out, decoder_2_out_7, and_1_out);
  Decoder #(.Selector_Bits(3)) decoder_2 (
    .sel(ramdualport_1_d[2:0]), .out_0(decoder_2_out_0), .out_1(decoder_2_out_1), .out_2(decoder_2_out_2),
    .out_4(decoder_2_out_4), .out_5(decoder_2_out_5), .out_6(decoder_2_out_6), .out_7(decoder_2_out_7));  // open: out_3
  LED led_54 (.in(jk_ff_27_q));
  LED led_55 (.in(jk_ff_26_q));
  and and_29 (and_29_out, not_17_out, or_9_out);
  or or_9 (or_9_out, or_10_out, decoder_3_out_4, decoder_3_out_0, decoder_3_out_6, decoder_3_out_2);
  or or_10 (or_10_out, decoder_3_out_1, decoder_3_out_7);
  and and_30 (and_30_out, ~decoder_3_out_7, and_1_out);  // And
  Multiplexer multiplexer_156 (.sel(not_11_out), .in_0(1'b1), .in_1(pulldown_43_out[18]), .out(multiplexer_156_out));
  or or_11 (or_11_out, decoder_2_out_7, decoder_2_out_0, decoder_2_out_2, decoder_2_out_1);
  // NotConnected on nothing
  LED led_56 (.in(jk_ff_25_q));
  Multiplexer multiplexer_157 (.sel(not_22_out), .in_0(and_29_out), .in_1(1'b1), .out(multiplexer_157_out));
  and and_31 (and_31_out, decoder_3_out_7, and_1_out);
  Decoder #(.Selector_Bits(3)) decoder_3 (
    .sel(ramdualport_1_d[2:0]), .out_0(decoder_3_out_0), .out_1(decoder_3_out_1), .out_2(decoder_3_out_2),
    .out_4(decoder_3_out_4), .out_5(decoder_3_out_5), .out_6(decoder_3_out_6), .out_7(decoder_3_out_7));  // open: out_3
  nor nor_1 (nor_1_out, multiplexer_126_out, multiplexer_127_out);
  nor nor_2 (nor_2_out, multiplexer_128_out, multiplexer_129_out);
  nor nor_3 (nor_3_out, multiplexer_130_out, multiplexer_131_out);
  nor nor_4 (nor_4_out, multiplexer_132_out, multiplexer_133_out);
  Multiplexer multiplexer_158 (
    .sel(not_11_out), .in_0(and_32_out), .in_1(pulldown_43_out[19]), .out(multiplexer_158_out));
  and and_32 (and_32_out, or_11_out, not_15_out);
  Multiplexer multiplexer_159 (.sel(not_22_out), .in_0(1'b1), .in_1(pulldown_43_out[12]), .out(multiplexer_159_out));
  and and_33 (and_33_out, or_12_out, not_17_out);
  or or_12 (or_12_out, decoder_3_out_7, decoder_3_out_0, decoder_3_out_2, decoder_3_out_1);
  // NotConnected on nothing
  Multiplexer multiplexer_160 (
    .sel(pulldown_43_out[26]), .in_0(d_ff_9_q), .in_1(and_40_out), .out(multiplexer_160_out));
  Multiplexer multiplexer_161 (
    .sel(pulldown_43_out[26]), .in_0(d_ff_10_q), .in_1(add_8_c_o), .out(multiplexer_161_out));
  Multiplexer multiplexer_162 (
    .sel(not_11_out), .in_0(and_34_out), .in_1(pulldown_43_out[20]), .out(multiplexer_162_out));
  and and_34 (and_34_out, not_15_out, or_13_out);
  or or_13 (or_13_out, decoder_2_out_7, and_26_out);
  Multiplexer multiplexer_163 (
    .sel(not_22_out), .in_0(and_33_out), .in_1(pulldown_43_out[13]), .out(multiplexer_163_out));
  and and_35 (and_35_out, not_17_out, or_14_out);
  or or_14 (or_14_out, decoder_3_out_7, and_30_out);
  and and_36 (and_36_out, nor_1_out, nor_2_out);
  and and_37 (and_37_out, nor_3_out, nor_4_out);
  D_FF d_ff_9 (.D(multiplexer_160_out), .C(not_10_out), .Q(d_ff_9_q));  // open: nQ
  D_FF d_ff_10 (.D(multiplexer_161_out), .C(not_10_out), .Q(d_ff_10_q));  // open: nQ
  Multiplexer multiplexer_164 (
    .sel(not_11_out), .in_0(and_38_out), .in_1(pulldown_43_out[21]), .out(multiplexer_164_out));
  and and_38 (and_38_out, not_15_out, or_15_out);
  or or_15 (or_15_out, decoder_2_out_6, decoder_2_out_5, decoder_2_out_1, and_28_out, decoder_2_out_0);
  Multiplexer multiplexer_165 (
    .sel(not_22_out), .in_0(and_35_out), .in_1(pulldown_43_out[14]), .out(multiplexer_165_out));
  and and_39 (and_39_out, not_17_out, or_16_out);
  or or_16 (or_16_out, decoder_3_out_6, decoder_3_out_5, decoder_3_out_1, and_31_out, decoder_3_out_0);
  and and_40 (and_40_out, and_36_out, and_37_out);
  not not_10 (not_10_out, CLK);
  Multiplexer multiplexer_166 (
    .sel(not_11_out), .in_0(and_41_out), .in_1(pulldown_43_out[22]), .out(multiplexer_166_out));
  and and_41 (and_41_out, not_15_out, or_17_out);
  or or_17 (or_17_out, decoder_2_out_5, decoder_2_out_0);
  Multiplexer multiplexer_167 (
    .sel(not_22_out), .in_0(and_39_out), .in_1(pulldown_43_out[15]), .out(multiplexer_167_out));
  and and_42 (and_42_out, not_17_out, or_18_out);
  not not_11 (not_11_out, not_19_out);
  not not_12 (not_12_out, pulldown_43_out[27]);
  not not_13 (not_13_out, not_12_out);
  not not_14 (not_14_out, not_13_out);
  not not_15 (not_15_out, not_14_out);
  Multiplexer multiplexer_168 (
    .sel(not_22_out), .in_0(and_42_out), .in_1(pulldown_43_out[16]), .out(multiplexer_168_out));
  not not_16 (not_16_out, not_23_out);
  not not_17 (not_17_out, not_16_out);
  or or_18 (or_18_out, decoder_3_out_5, decoder_3_out_0);
  not not_18 (not_18_out, not_20_out);
  not not_19 (not_19_out, not_18_out);
  not not_20 (not_20_out, not_21_out);
  not not_21 (not_21_out, pulldown_43_out[27]);
  not not_22 (not_22_out, not_26_out);
  not not_23 (not_23_out, not_24_out);
  not not_24 (not_24_out, pulldown_43_out[28]);
  not not_25 (not_25_out, not_27_out);
  not not_26 (not_26_out, not_25_out);
  not not_27 (not_27_out, not_28_out);
  not not_28 (not_28_out, pulldown_43_out[28]);

  // Notes on the sheet:
  //   CLK: Hz: 50
  //   ENDEF
  //   Bad hack,
  //   here to make sure rom isn't activated
  //   with wrong address, causing
  //   control line bursts
  //   which can be bad for some components
  //   ( registers i'm looking at you )
  //   DEF
  //   T-Flip-Flop mode is only on 
  //   when both INMOD and ENIN
  //   are enabled,
  //   if any one of those is off 
  //   T Flip-Flop mode is off.
  //   CF
  //   ZF
  //   INMOD
  //   LOAD
  //   Note to future self,
  //   if we add something 
  //   else to the rom on jmpz/jmpc, 
  //   then we need to make sure 
  //   it is overriden correctly here!!!
  //   This is why the step 3 and 4 
  //   plexers are important!!!
  //   CLKMOD
  //   CLK
  //   Bad hack to wait
  //   for PC to increment
  //   before loading to MAR,
  //   in MICROSTEP2,
  //   delay amount was found
  //   by trial and error
  //   CASCADEMOD
  //   EXTERNALBUSIN
  //   ENO
  //   Both 3 and 4,
  //   override the default to add one to pc
  //   which happens normally.
  //   ENIN
  //   Step 3
  //   Step 4
  //   contents of rom_1 (hex, n*v repeats v):
  //   0,1000588,1000588,4000000,41c0000,1000588,1000588,0,12000000,a000000,4000000,0,0,
  //   0,580,580,0,1004780,1100780,1804000,1824000,28007c0,38007c0,1000200,16000000,e000000,
  //   21804000,0,0,0,780,780
  //   MAR
  //   IR
  //   INTERNALBUSOUT
  //   Bus data injector/probe
  //   Rationale for the AND gate at INMOD and ENIN of the JK flip-lfop registers:
  //   -------------------------------------------
  //   If INMOD = 1, but ENIN = 0, 
  //   then, even though you have requested T Flip-Flop mode, your request cannot be completed
  //   because you need D Flip-Flop mode to fullfill ENIN = 0, a.k.a to make sure the ouput
  //   dosen't change on clock pulse.
  //   If INMOD = 0, but ENIN = whatever,
  //   then you have requested D Flip-Flop mode, and since D Flip-Flop mode
  //   works no matter what ENIN is, we can just enable D Flip-Flop mode.
  //   Therfore
  //   you want only INMOD = 1 and ENIN = 1 to enable T Flip-Flop mode otherwise 
  //   you want D Flip-Flop mode
  //   CIN
  //   AND
  //   Microinstruction step 3 and 4
  //   combinatorial logic,
  //   yes, i know connecting up the multiplexers
  //   like this makes them act like or gates
  //   and i could replace them with or gates,
  //   however i think this makes more sense
  //   and it's pretty trivial to optimise this if needed.
  //   Register A
  //   Register B
  //   ALU
  //   PC
  //   DEF, INMOD, LOAD, CLKMOD, CASCADEMOD
  //   ENDEF is always on when
  //   ACNTRLLINEMOD is on
endmodule
